// Digital circuit _CPU.dig as structural Verilog
module CPU (
  input  Clk_Slow,
  input  Clk_Fast,
  input  Clk_Manual
);

  wire alu_1_z, and_2_out, and_3_out, BR_taken, Branch, counter_3_ovf, counter_4_ovf, CPU_Clock, CPU_Reset,
       Debug_out, delay_1_out, dipswitch_33_out, dipswitch_34_out, dipswitch_35_out, Exe_MemRd, Exe_rd,
       Exe_we, Fast_out, Halt_2_out, ID_stall, instr_decoder_1_b_mux, instr_decoder_1_branch,
       instr_decoder_1_mem_rd, instr_decoder_1_mem_wr, instr_decoder_1_valid, instr_decoder_1_wb_we, Jump,
       Manual_out, Mem_rd, Mem_we, nand_1_out, not_1_out, not_2_out, not_3_out, not_4_out, not_5_out,
       not_6_out, or_2_out, or_3_out, pipe_exe_mem_1_p5, pipe_exe_mem_1_p6, pipe_exe_mem_1_p7,
       pipe_exe_mem_1_p8, pipe_exe_mem_1_p9, pipe_id_exe_1_p6, pipe_id_exe_1_p7, pipe_id_exe_1_p8,
       pipe_id_exe_1_p9, pipe_id_exe_1_p10, pipe_id_exe_1_p12, pipe_id_exe_1_p13, pipe_mem_wb_1_p4,
       pipe_mem_wb_1_p5, pipe_mem_wb_1_p6, pipectrl_1__1cc, pipectrl_1_led_busy, pipectrl_1_led_empty,
       pipectrl_1_led_valid, pipectrl_1_led_waiting, pipectrl_1_reg_clear, pipectrl_1_reg_clock,
       pipectrl_1_reg_oe, pipectrl_1_valid__this, pipectrl_2_led_busy, pipectrl_2_led_empty,
       pipectrl_2_led_valid, pipectrl_2_led_waiting, pipectrl_2_ready__prev, pipectrl_2_reg_clear,
       pipectrl_2_reg_clock, pipectrl_2_reg_oe, pipectrl_2_valid__this, pipectrl_3__1cc, pipectrl_3_led_busy,
       pipectrl_3_led_empty, pipectrl_3_led_valid, pipectrl_3_led_waiting, pipectrl_3_ready__prev,
       pipectrl_3_valid__this, pipectrl_4__1cc, pipectrl_4_led_busy, pipectrl_4_led_empty,
       pipectrl_4_led_valid, pipectrl_4_led_waiting, pipectrl_4_ready__prev, pipectrl_4_valid__this,
       pipectrl_5__1cc, pipectrl_5_led_busy, pipectrl_5_led_empty, pipectrl_5_led_valid,
       pipectrl_5_led_waiting, pipectrl_5_ready__prev, pipectrl_5_valid__this, pipereg_mem_1_p5,
       pipereg_mem_1_p6, pipereg_mem_1_p8, pipereg_mem_2_p7, pipereg_mem_2_p8, pipereg_wb_3_p3, pullup_1_out,
       pullup_2_out, PwrOn_Reset_out, Reset_out, rs_ff_as_1_q, RVC_enabled_out, Slow_out;
  wire [0:0] instr_decoder_1_a_mux;
  wire [1:0] A_mux, B_mux, instr_decoder_1_br_ctrl, instr_decoder_1_j_ctrl, instr_decoder_1_mem_mux,
       pipereg_branch_1_p4, pipereg_mem_2_p5;
  wire [2:0] instr_decoder_1_imm_ctrl, instr_decoder_1_mem_sz, pipereg_mem_2_p6;
  wire [2:1] to_b_of_PC_adder;
  wire [3:0] multiplexer_7_out, pulldown_2_out;
  wire [4:0] ID_Rs1, ID_Rs2, instr_decoder_1_alu_ctrl, instr_decoder_1_wb_reg, pipereg_exe_1_p2,
       pipereg_wb_3_p4;
  wire [29:0] regfile_1_disp_r0, regfile_1_disp_r1, regfile_1_disp_r2, regfile_1_disp_r3, regfile_1_disp_r4,
       regfile_1_disp_r5, regfile_1_disp_r6, regfile_1_disp_r7, regfile_1_disp_r8, regfile_1_disp_r9,
       regfile_1_disp_r10, regfile_1_disp_r11, regfile_1_disp_r12, regfile_1_disp_r13, regfile_1_disp_r14,
       regfile_1_disp_r15, regfile_1_disp_r16, regfile_1_disp_r17, regfile_1_disp_r18, regfile_1_disp_r19,
       regfile_1_disp_r20, regfile_1_disp_r21, regfile_1_disp_r22, regfile_1_disp_r23, regfile_1_disp_r24,
       regfile_1_disp_r25, regfile_1_disp_r26, regfile_1_disp_r27, regfile_1_disp_r28, regfile_1_disp_r29,
       regfile_1_disp_r30, regfile_1_disp_r31;
  wire [31:0] basicadder_1_y, BR_addr, counter_1_out, counter_2_out, counter_3_out, counter_4_out, Data_d,
       dipswitch_32_out, Exe_data, imm_decoder_1_imm, instr, J_addr, Mem_data, mem_ext_1_out,
       multiplexer_1_out, multiplexer_2_out, multiplexer_3_out, multiplexer_4_out, multiplexer_5_out,
       multiplexer_6_out, pipe_exe_mem_1_p10, pipe_exe_mem_1_p11, pipe_exe_mem_1_p12, pipe_id_exe_1_p11,
       pipe_id_exe_1_p14, pipe_if_id_1_instr_disp, pipe_if_id_1_instr_out, pipe_if_id_1_pc_disp,
       pipe_if_id_1_pc_nextdisp, pipe_if_id_1_pc_nextout, pipe_if_id_1_pc_out, pipe_mem_wb_1_p7,
       pipe_pc_1_pc_disp, pipe_pc_1_pc_out, Progr_d, regfile_1_rd1, regfile_1_rd2, undriven, undriven_2;

  DipSwitch dipswitch_1 (.out(dipswitch_32_out[31]));
  DipSwitch dipswitch_2 (.out(dipswitch_32_out[30]));
  DipSwitch dipswitch_3 (.out(dipswitch_32_out[29]));
  // Probe on {{29{1'b0}}, to_b_of_PC_adder, 1'b0}
  DipSwitch dipswitch_4 (.out(dipswitch_32_out[28]));
  DipSwitch dipswitch_5 (.out(dipswitch_32_out[27]));
  DipSwitch dipswitch_6 (.out(dipswitch_32_out[26]));
  DipSwitch dipswitch_7 (.out(dipswitch_32_out[25]));
  DipSwitch dipswitch_8 (.out(dipswitch_32_out[24]));
  DipSwitch dipswitch_9 (.out(dipswitch_32_out[23]));
  DipSwitch dipswitch_10 (.out(dipswitch_32_out[22]));
  DipSwitch dipswitch_11 (.out(dipswitch_32_out[21]));
  DipSwitch dipswitch_12 (.out(dipswitch_32_out[20]));
  DipSwitch dipswitch_13 (.out(dipswitch_32_out[19]));
  DipSwitch dipswitch_14 (.out(dipswitch_32_out[18]));
  DipSwitch dipswitch_15 (.out(dipswitch_32_out[17]));
  or or_1 (to_b_of_PC_adder[2], not_1_out, and_2_out);
  not not_1 (not_1_out, to_b_of_PC_adder[1]);
  and and_1 (to_b_of_PC_adder[1], RVC_enabled_out, not_2_out);
  DipSwitch RVC_enabled (.out(RVC_enabled_out));
  DipSwitch dipswitch_16 (.out(dipswitch_32_out[16]));
  DipSwitch dipswitch_17 (.out(dipswitch_32_out[15]));
  DipSwitch dipswitch_18 (.out(dipswitch_32_out[14]));
  DipSwitch dipswitch_19 (.out(dipswitch_32_out[13]));
  not not_2 (not_2_out, and_2_out);
  DipSwitch dipswitch_20 (.out(dipswitch_32_out[12]));
  DipSwitch dipswitch_21 (.out(dipswitch_32_out[11]));
  DipSwitch dipswitch_22 (.out(dipswitch_32_out[10]));
  DipSwitch dipswitch_23 (.out(dipswitch_32_out[9]));
  and and_2 (and_2_out, instr[0], instr[1]);
  DipSwitch dipswitch_24 (.out(dipswitch_32_out[8]));
  DipSwitch dipswitch_25 (.out(dipswitch_32_out[7]));
  DipSwitch dipswitch_26 (.out(dipswitch_32_out[6]));
  DipSwitch dipswitch_27 (.out(dipswitch_32_out[5]));
  DipSwitch dipswitch_28 (.out(dipswitch_32_out[4]));
  DipSwitch dipswitch_29 (.out(dipswitch_32_out[3]));
  DipSwitch dipswitch_30 (.out(dipswitch_32_out[2]));
  DipSwitch #(.dipDefault("true")) dipswitch_31 (.out(dipswitch_32_out[1]));
  // Probe on dipswitch_32_out
  DipSwitch #(.dipDefault("true")) dipswitch_32 (.out(dipswitch_32_out[0]));
  // Probe on multiplexer_1_out
  // Probe on multiplexer_2_out
  Multiplexer #(.Selector_Bits(2), .Bits(32)) multiplexer_1 (
    .sel({Jump, BR_taken}), .in_0(basicadder_1_y), .in_1(BR_addr), .in_2(J_addr), .in_3({32{1'b0}}),
    .out(multiplexer_1_out));
  Multiplexer #(.Bits(32)) multiplexer_2 (
    .sel(rs_ff_as_1_q), .in_0(32'h100), .in_1(multiplexer_1_out), .out(multiplexer_2_out));
  Pipe_PC pipe_pc_1 (
    .PC_in(multiplexer_2_out), .PC_out(pipe_pc_1_pc_out), .PC_disp(pipe_pc_1_pc_disp),
    .REGin_Clear(pipectrl_1_reg_clear), .REGin_Clock(pipectrl_1_reg_clock), .REGin_OE(pipectrl_1_reg_oe));
  PipeCtrl pipectrl_1 (
    .Valid__this(pipectrl_1_valid__this), .Ready__next(pipectrl_2_ready__prev),
    .Done__this(dipswitch_33_out), ._1cc(pipectrl_1__1cc), .Clock(CPU_Clock), .Reset(CPU_Reset),
    .Flush(or_2_out), .REG_Clear(pipectrl_1_reg_clear), .REG_Clock(pipectrl_1_reg_clock),
    .REG_OE(pipectrl_1_reg_oe), .LED_Valid(pipectrl_1_led_valid), .LED_Busy(pipectrl_1_led_busy),
    .LED_Waiting(pipectrl_1_led_waiting), .LED_Empty(pipectrl_1_led_empty));  // open: Valid__prev, Ready__prev
  not not_3 (not_3_out, CPU_Reset);
  LED led_1 (.in(or_2_out));
  RS_FF_AS rs_ff_as_1 (.S(pipectrl_1_valid__this), .R(not_3_out), .Q(rs_ff_as_1_q));  // open: nQ
  LED Busy (.in(pipectrl_1_led_busy));
  LED Valid (.in(pipectrl_1_led_valid));
  or or_2 (or_2_out, BR_taken, Jump);
  Button #(.activeLow("true")) Manual (.out(Manual_out));
  Button #(.activeLow("true")) Slow (.out(Slow_out));
  Button #(.activeLow("true")) Fast (.out(Fast_out));
  LED Halt (.in(not_4_out));
  not not_4 (not_4_out, pullup_2_out);
  BasicAdder basicadder_1 (.A(pipe_pc_1_pc_out), .B(32'h4), .Y(basicadder_1_y));
  // Probe on pipe_pc_1_pc_disp
  LED Wait (.in(pipectrl_1_led_waiting));
  LED Empty (.in(pipectrl_1_led_empty));
  ClockCtrl clockctrl_1 (
    .Sel_Man(Manual_out), .Clk_Man(Clk_Manual), .Sel_Slow(Slow_out), .Clk_Slow(Clk_Slow),
    .Sel_Fast(Fast_out), .Clk_Fast(Clk_Fast), .Halt(pullup_2_out), .Reset(pullup_1_out), .Clk_Out(CPU_Clock));
  LED led_2 (.in(pipectrl_1__1cc));
  DipSwitch #(.dipDefault("true")) dipswitch_33 (.out(dipswitch_33_out));
  // PolarityAwareLED polarityawareled_1: pin names not known; wires that end beside it: CPU_Clock, 1'b0
  PullUp pullup_1 (.out(pullup_1_out));
  PullUp pullup_2 (.out(pullup_2_out));
  ROM #(.AddrBits(16), .Bits(32)) Progr (.A(pipe_pc_1_pc_out[17:2]), .sel(1'b1), .D(Progr_d));
  Reset_Unit reset_unit_1 (.Clock(CPU_Clock), .Reset_In(pullup_1_out), .Reset_Out(CPU_Reset));
  PFET pfet_1 (.G(PwrOn_Reset_out), .S(1'b0), .D(pullup_1_out));
  PFET pfet_2 (.G(Reset_out), .S(1'b0), .D(pullup_1_out));
  PFET pfet_3 (.G(Halt_2_out), .S(1'b0), .D(pullup_2_out));
  Reset PwrOn_Reset (.out(PwrOn_Reset_out));
  Button #(.activeLow("true")) Reset (.out(Reset_out));
  Button #(.activeLow("true")) Halt_2 (.out(Halt_2_out));
  assign instr = ~Debug_out ? Progr_d : 32'bz;  // DriverInvSel driverinvsel_1
  assign instr = Debug_out ? dipswitch_32_out : 32'bz;  // Driver driver_1
  PullDown #(.Bits(32)) pulldown_1 (.out(instr));
  DipSwitch Debug (.out(Debug_out));
  // PolarityAwareLED polarityawareled_2: pin names not known; wires that end beside it: 1'b1, CPU_Reset
  Pipe_IF_ID pipe_if_id_1 (
    .PC_in(pipe_pc_1_pc_out), .Instr_in(instr), .PC_out(pipe_if_id_1_pc_out), .PC_disp(pipe_if_id_1_pc_disp),
    .Instr_out(pipe_if_id_1_instr_out), .Instr_disp(pipe_if_id_1_instr_disp),
    .REGin_Clear(pipectrl_2_reg_clear), .REGin_Clock(pipectrl_2_reg_clock), .REGin_OE(pipectrl_2_reg_oe),
    .PC_nextin(basicadder_1_y), .PC_nextout(pipe_if_id_1_pc_nextout), .PC_nextdisp(pipe_if_id_1_pc_nextdisp));  // open: REGout_Clock, REGout_OE, REGout_Clear
  PipeCtrl pipectrl_2 (
    .Valid__prev(pipectrl_1_valid__this), .Ready__prev(pipectrl_2_ready__prev),
    .Valid__this(pipectrl_2_valid__this), .Ready__next(pipectrl_3_ready__prev), .Done__this(ID_stall),
    .Clock(CPU_Clock), .Reset(CPU_Reset), .Flush(BR_taken), .REG_Clear(pipectrl_2_reg_clear),
    .REG_Clock(pipectrl_2_reg_clock), .REG_OE(pipectrl_2_reg_oe), .LED_Valid(pipectrl_2_led_valid),
    .LED_Busy(pipectrl_2_led_busy), .LED_Waiting(pipectrl_2_led_waiting), .LED_Empty(pipectrl_2_led_empty));  // open: _1cc
  LED Valid_2 (.in(pipectrl_2_led_valid));
  LED led_3 (.in(BR_taken));
  LED Busy_2 (.in(pipectrl_2_led_busy));
  LED Wait_2 (.in(pipectrl_2_led_waiting));
  // Probe on pipe_if_id_1_pc_disp
  // Probe on pipe_if_id_1_pc_nextdisp
  // Probe on pipe_if_id_1_instr_disp
  LED Empty_2 (.in(pipectrl_2_led_empty));
  PFET pfet_4 (.G(nand_1_out), .S(1'b0), .D(pullup_2_out));
  Instr_Decoder instr_decoder_1 (
    .Inst(pipe_if_id_1_instr_out), .Valid(instr_decoder_1_valid), .J_ctrl(instr_decoder_1_j_ctrl),
    .Jump(Jump), .Rs1(ID_Rs1), .Rs2(ID_Rs2), .A_mux(instr_decoder_1_a_mux[0]), .B_mux(instr_decoder_1_b_mux),
    .Imm_ctrl(instr_decoder_1_imm_ctrl), .Branch(instr_decoder_1_branch), .BR_ctrl(instr_decoder_1_br_ctrl),
    .ALU_ctrl(instr_decoder_1_alu_ctrl), .Mem_mux(instr_decoder_1_mem_mux), .Mem_sz(instr_decoder_1_mem_sz),
    .Mem_rd(instr_decoder_1_mem_rd), .Mem_wr(instr_decoder_1_mem_wr), .WB_we(instr_decoder_1_wb_we),
    .WB_reg(instr_decoder_1_wb_reg));
  nand nand_1 (nand_1_out, ~instr_decoder_1_valid, pipectrl_2_valid__this);  // NAnd
  RegFile regfile_1 (
    .Rs1(ID_Rs1), .Rs2(ID_Rs2), .Ws(pipereg_wb_3_p4), .Rd1(regfile_1_rd1), .Rd2(regfile_1_rd2),
    .Clock(CPU_Clock), .Reset(CPU_Reset), .Data(pipe_mem_wb_1_p7), .We(pipereg_wb_3_p3),
    .Disp_R0(regfile_1_disp_r0), .Disp_R1(regfile_1_disp_r1), .Disp_R2(regfile_1_disp_r2),
    .Disp_R3(regfile_1_disp_r3), .Disp_R4(regfile_1_disp_r4), .Disp_R5(regfile_1_disp_r5),
    .Disp_R6(regfile_1_disp_r6), .Disp_R7(regfile_1_disp_r7), .Disp_R8(regfile_1_disp_r8),
    .Disp_R9(regfile_1_disp_r9), .Disp_R10(regfile_1_disp_r10), .Disp_R11(regfile_1_disp_r11),
    .Disp_R12(regfile_1_disp_r12), .Disp_R13(regfile_1_disp_r13), .Disp_R14(regfile_1_disp_r14),
    .Disp_R15(regfile_1_disp_r15), .Disp_R16(regfile_1_disp_r16), .Disp_R17(regfile_1_disp_r17),
    .Disp_R18(regfile_1_disp_r18), .Disp_R19(regfile_1_disp_r19), .Disp_R20(regfile_1_disp_r20),
    .Disp_R21(regfile_1_disp_r21), .Disp_R22(regfile_1_disp_r22), .Disp_R23(regfile_1_disp_r23),
    .Disp_R24(regfile_1_disp_r24), .Disp_R25(regfile_1_disp_r25), .Disp_R26(regfile_1_disp_r26),
    .Disp_R27(regfile_1_disp_r27), .Disp_R28(regfile_1_disp_r28), .Disp_R29(regfile_1_disp_r29),
    .Disp_R30(regfile_1_disp_r30), .Disp_R31(regfile_1_disp_r31));
  // FowardUnit Forwarding_Unit: pin names not known; wires that end beside it: ID_stall, ID_Rs1, ID_Rs2, A_mux, B_mux, Exe_rd, Exe_we, Exe_MemRd, Mem_rd, Mem_we
  Imm_Decoder imm_decoder_1 (.Ctrl(instr_decoder_1_imm_ctrl), .Inst(pipe_if_id_1_instr_out), .Imm(imm_decoder_1_imm));
  // Probe on regfile_1_disp_r0
  // Probe on regfile_1_disp_r1
  // Probe on regfile_1_disp_r2
  // Probe on regfile_1_disp_r3
  // Probe on regfile_1_disp_r4
  // Probe on regfile_1_disp_r5
  // Probe on regfile_1_disp_r6
  // Probe on regfile_1_disp_r7
  // Probe on regfile_1_disp_r8
  // Probe on regfile_1_disp_r9
  // Probe on regfile_1_disp_r10
  // Probe on regfile_1_disp_r11
  // Probe on regfile_1_disp_r12
  // Probe on regfile_1_disp_r13
  // Probe on regfile_1_disp_r14
  // Probe on regfile_1_disp_r15
  not not_5 (not_5_out, ID_stall);
  // Probe on regfile_1_disp_r16
  // Probe on regfile_1_disp_r17
  // Probe on regfile_1_disp_r18
  // Probe on regfile_1_disp_r19
  // Probe on regfile_1_disp_r20
  // Probe on regfile_1_disp_r21
  // Probe on regfile_1_disp_r22
  // Probe on regfile_1_disp_r23
  // Probe on regfile_1_disp_r24
  // Probe on regfile_1_disp_r25
  // Probe on regfile_1_disp_r26
  // Probe on regfile_1_disp_r27
  // Probe on regfile_1_disp_r28
  // Probe on regfile_1_disp_r29
  // Probe on regfile_1_disp_r30
  // Probe on regfile_1_disp_r31
  LED MemRead_in_EXE (.in(not_5_out));
  LED Stage__EXE (.in(A_mux[0]));
  LED Stage__MEM (.in(A_mux[1]));
  LED Stage__EXE_2 (.in(B_mux[0]));
  LED Stage__MEM_2 (.in(B_mux[1]));
  Jump_Unit jump_unit_1 (
    .J_addr(J_addr), .J_ctrl(instr_decoder_1_j_ctrl), .Imm(imm_decoder_1_imm), .Rs1(multiplexer_3_out),
    .PC(pipe_if_id_1_pc_out));
  Multiplexer #(.Selector_Bits(2), .Bits(32)) multiplexer_3 (
    .sel(A_mux), .in_0(regfile_1_rd1), .in_1(Exe_data), .in_2(Mem_data), .in_3({32{1'b0}}),
    .out(multiplexer_3_out));
  Multiplexer #(.Selector_Bits(2), .Bits(32)) multiplexer_4 (
    .sel(B_mux), .in_0(regfile_1_rd2), .in_1(Exe_data), .in_2(Mem_data), .in_3({32{1'b0}}),
    .out(multiplexer_4_out));
  Multiplexer #(.Selector_Bits(2), .Bits(32)) multiplexer_5 (
    .sel({Jump, instr_decoder_1_a_mux[0]}), .in_0(multiplexer_3_out), .in_1(pipe_if_id_1_pc_out),
    .in_2(pipe_if_id_1_pc_nextout), .in_3({32{1'b0}}), .out(multiplexer_5_out));
  Multiplexer #(.Bits(32)) multiplexer_6 (
    .sel(instr_decoder_1_b_mux), .in_0(multiplexer_4_out), .in_1(imm_decoder_1_imm), .out(multiplexer_6_out));
  // PipeReg_Branch pipereg_branch_1: pin names not known; wires that end beside it: instr_decoder_1_branch, instr_decoder_1_br_ctrl, Branch, pipereg_branch_1_p4
  // PipeReg_EXE pipereg_exe_1: pin names not known; wires that end beside it: instr_decoder_1_alu_ctrl, pipereg_exe_1_p2
  // PipeReg_MEM pipereg_mem_1: pin names not known; wires that end beside it: instr_decoder_1_mem_mux, instr_decoder_1_mem_sz, instr_decoder_1_mem_rd, instr_decoder_1_mem_wr, pipereg_mem_1_p5, pipereg_mem_1_p6, Exe_MemRd, pipereg_mem_1_p8
  // PipeReg_WB pipereg_wb_1: pin names not known; wires that end beside it: instr_decoder_1_wb_we, instr_decoder_1_wb_reg, Exe_we, Exe_rd
  // Pipe_ID_EXE pipe_id_exe_1: pin names not known; wires that end beside it: pipe_if_id_1_pc_out, pipe_if_id_1_pc_nextout, multiplexer_4_out, multiplexer_5_out, multiplexer_6_out, pipe_id_exe_1_p6, pipe_id_exe_1_p7, pipe_id_exe_1_p8, pipe_id_exe_1_p9, pipe_id_exe_1_p10, pipe_id_exe_1_p11, pipe_id_exe_1_p12, pipe_id_exe_1_p13, pipe_id_exe_1_p14
  PipeCtrl pipectrl_3 (
    .Valid__prev(pipectrl_2_valid__this), .Ready__prev(pipectrl_3_ready__prev),
    .Valid__this(pipectrl_3_valid__this), .Ready__next(pipectrl_4_ready__prev),
    .Done__this(dipswitch_34_out), ._1cc(pipectrl_3__1cc), .Clock(CPU_Clock), .Reset(CPU_Reset),
    .LED_Valid(pipectrl_3_led_valid), .LED_Busy(pipectrl_3_led_busy), .LED_Waiting(pipectrl_3_led_waiting),
    .LED_Empty(pipectrl_3_led_empty));  // open: Flush, REG_Clear, REG_Clock, REG_OE
  LED Valid_3 (.in(pipectrl_3_led_valid));
  LED Busy_3 (.in(pipectrl_3_led_busy));
  LED Wait_3 (.in(pipectrl_3_led_waiting));
  // Probe on pipe_id_exe_1_p6
  // Probe on pipe_id_exe_1_p7
  // Probe on pipe_id_exe_1_p8
  // Probe on pipe_id_exe_1_p9
  // Probe on pipe_id_exe_1_p10
  // Probe on nothing
  LED led_4 (.in(pipectrl_3__1cc));
  LED Empty_3 (.in(pipectrl_3_led_empty));
  ALU alu_1 (.ALU_ctrl(multiplexer_7_out), .A(pipe_id_exe_1_p14), .B(undriven), .Y(Exe_data), .Z(alu_1_z));
  PullDown #(.Bits(4)) pulldown_2 (.out(pulldown_2_out));
  DipSwitch #(.dipDefault("true")) dipswitch_34 (.out(dipswitch_34_out));
  Multiplexer #(.Bits(4)) multiplexer_7 (
    .sel(pipereg_exe_1_p2[4]), .in_0(pipereg_exe_1_p2[3:0]), .in_1(pulldown_2_out), .out(multiplexer_7_out));
  Branch_Unit branch_unit_1 (
    .Imm(undriven_2), .PC(pipe_id_exe_1_p11), .Branch(Branch), .BR_ctrl(pipereg_branch_1_p4),
    .ALU_zero(alu_1_z), .ALU_SLT(Exe_data[0]), .BR_addr(BR_addr), .BR_taken(BR_taken));
  // PipeReg_MEM pipereg_mem_2: pin names not known; wires that end beside it: pipereg_mem_1_p5, pipereg_mem_1_p6, Exe_MemRd, pipereg_mem_1_p8, pipereg_mem_2_p5, pipereg_mem_2_p6, pipereg_mem_2_p7, pipereg_mem_2_p8
  // PipeReg_WB pipereg_wb_2: pin names not known; wires that end beside it: Exe_we, Exe_rd, Mem_we, Mem_rd
  // Pipe_EXE_MEM pipe_exe_mem_1: pin names not known; wires that end beside it: pipe_id_exe_1_p11, pipe_id_exe_1_p12, pipe_id_exe_1_p13, Exe_data, pipe_exe_mem_1_p5, pipe_exe_mem_1_p6, pipe_exe_mem_1_p7, pipe_exe_mem_1_p8, pipe_exe_mem_1_p9, pipe_exe_mem_1_p10, pipe_exe_mem_1_p11, pipe_exe_mem_1_p12, pipereg_mem_2_p6
  PipeCtrl pipectrl_4 (
    .Valid__prev(pipectrl_3_valid__this), .Ready__prev(pipectrl_4_ready__prev),
    .Valid__this(pipectrl_4_valid__this), .Ready__next(pipectrl_5_ready__prev),
    .Done__this(dipswitch_35_out), ._1cc(pipectrl_4__1cc), .Clock(CPU_Clock), .Reset(CPU_Reset),
    .LED_Valid(pipectrl_4_led_valid), .LED_Busy(pipectrl_4_led_busy), .LED_Waiting(pipectrl_4_led_waiting),
    .LED_Empty(pipectrl_4_led_empty));  // open: Flush, REG_Clear, REG_Clock, REG_OE
  LED Valid_4 (.in(pipectrl_4_led_valid));
  LED Busy_4 (.in(pipectrl_4_led_busy));
  LED Wait_4 (.in(pipectrl_4_led_waiting));
  LED Empty_4 (.in(pipectrl_4_led_empty));
  // Probe on pipe_exe_mem_1_p5
  // Probe on pipe_exe_mem_1_p6
  // Probe on pipe_exe_mem_1_p7
  // Probe on pipe_exe_mem_1_p8
  LED led_5 (.in(pipectrl_4__1cc));
  DipSwitch #(.dipDefault("true")) dipswitch_35 (.out(dipswitch_35_out));
  RAMDualPort #(.AddrBits(14), .Bits(32)) Data (
    .A(pipe_exe_mem_1_p12[13:0]), .Din(pipe_exe_mem_1_p11), .str(pipereg_mem_2_p8), .C(delay_1_out),
    .ld(pipereg_mem_2_p7), .D(Data_d));
  Delay #(.delayTime(2)) delay_1 (.in(pipereg_mem_2_p8), .out(delay_1_out));
  Mem_Ext mem_ext_1 (.size(pipereg_mem_2_p6), .in(Data_d), .out(mem_ext_1_out));
  Multiplexer #(.Selector_Bits(2), .Bits(32)) multiplexer_8 (
    .sel(pipereg_mem_2_p5), .in_0(pipe_exe_mem_1_p12), .in_1(mem_ext_1_out), .in_2(pipe_exe_mem_1_p10),
    .in_3({32{1'b0}}), .out(Mem_data));
  // Probe on counter_1_out
  // Probe on counter_3_out
  // Probe on counter_2_out
  // Probe on counter_4_out
  Counter #(.Bits(32)) counter_1 (
    .en(counter_3_ovf), .C(CPU_Clock), .clr(not_6_out), .out(counter_1_out));  // open: ovf
  Counter #(.Bits(32)) counter_2 (.en(counter_4_ovf), .C(or_3_out), .clr(not_6_out), .out(counter_2_out));  // open: ovf
  // PipeReg_WB pipereg_wb_3: pin names not known; wires that end beside it: Mem_we, Mem_rd, pipereg_wb_3_p3, pipereg_wb_3_p4
  // Pipe_MEM_WB pipe_mem_wb_1: pin names not known; wires that end beside it: pipe_exe_mem_1_p9, pipe_exe_mem_1_p10, Mem_data, pipe_mem_wb_1_p4, pipe_mem_wb_1_p5, pipe_mem_wb_1_p6, pipe_mem_wb_1_p7
  PipeCtrl pipectrl_5 (
    .Valid__prev(pipectrl_4_valid__this), .Ready__prev(pipectrl_5_ready__prev),
    .Valid__this(pipectrl_5_valid__this), ._1cc(pipectrl_5__1cc), .Clock(CPU_Clock), .Reset(CPU_Reset),
    .LED_Valid(pipectrl_5_led_valid), .LED_Busy(pipectrl_5_led_busy), .LED_Waiting(pipectrl_5_led_waiting),
    .LED_Empty(pipectrl_5_led_empty));  // open: Ready__next, Done__this, Flush, REG_Clear, REG_Clock, REG_OE
  LED Valid_5 (.in(pipectrl_5_led_valid));
  LED Busy_5 (.in(pipectrl_5_led_busy));
  LED Wait_5 (.in(pipectrl_5_led_waiting));
  LED Empty_5 (.in(pipectrl_5_led_empty));
  Counter #(.Bits(32)) counter_3 (.en(1'b1), .C(CPU_Clock), .clr(not_6_out), .out(counter_3_out), .ovf(counter_3_ovf));
  Counter #(.Bits(32)) counter_4 (
    .en(pipectrl_5_valid__this), .C(or_3_out), .clr(not_6_out), .out(counter_4_out), .ovf(counter_4_ovf));
  // Probe on pipe_mem_wb_1_p4
  // Probe on pipe_mem_wb_1_p5
  // Probe on pipe_mem_wb_1_p6
  not not_6 (not_6_out, CPU_Reset);
  or or_3 (or_3_out, pipectrl_5__1cc, and_3_out);
  and and_3 (and_3_out, CPU_Clock, not_6_out);

  // Notes on the sheet:
  //   Clk_Slow: Hz: 2
  //   Clk_Fast: Hz: 2147483647
  //   func7
  //   TODO:
  //   - Rework Clock Unit
  //   - Memory interface
  //   - Instruction cache
  //   - Check Addr of Instr before MemWrite
  //   Later:
  //   - User/Superviser/Machine mode
  //   - Interupts
  //   - Exceptions
  //   - CSR's
  //   - Memory Protection
  //   - Memory Management
  //   - RVC Decoding
  //   Rework:
  //   - Clear pulse in PipeCtrl
  //   RVC-PC-Increment
  //   rs2
  //   rs1
  //   func3
  //   rd
  //   opcode
  //   11
  //   Jump/Branch-Unit
  //   Reset-Vector
  //   Clock / Reset / Halt
  //   Instruction-Fetch
  //   contents of Progr (hex, n*v repeats v):
  //   64*0,1000593,613
  //   Branch-Unit
  //   Instruction-Decode / Register-Fetch
  //   Forwarding-Unit
  //   Stall
  //   Rs1 forward from:
  //   Rs2 forward from:
  //   Jump-Unit
  //   A_mux
  //   00: Rs1
  //   01: PC
  //   10: PC_next
  //   B_mux
  //   0: Rs2
  //   1: Imm
  //   Execute
  //   MUL/DIV-mode
  //   Memory
  //   Mem_sz
  //   Basic Cycle Counter
  //   Basic Instr. Counter
  //   Mem_mux
  //   00: ALU
  //   01: Mem
  //   10: PC_next
  //   Write-Back
endmodule
